// Logisim project ckt.circ as structural Verilog: 1 circuit, main circuit main
module main (
  input  x0,
  input  x1,
  input  x2
);

  wire A_out, not_1_out, O_out;

  not not_1 (not_1_out, x2);
  and A (A_out, x1, not_1_out);
  LED led_1 (.in(O_out));
  or O (O_out, x0, A_out);

  // Notes on the sheet:
  //   notX2
  //   w1
  //   y
endmodule
