// Logisim project ckt.circ as structural Verilog: 1 circuit, main circuit main
module main (
  input  x4,
  input  x3,
  input  x2,
  input  x1,
  input  x0
);

  wire a_out, multiplexer_1_out, nor_out, not_1_out, not_2_out;

  not not_1 (not_1_out, x0);
  and a (a_out, x0, x1);
  not not_2 (not_2_out, nor_out);
  nor \nor  (nor_out, x0, x1);
  Multiplexer #(.select(3), .enable("false")) multiplexer_1 (
    .in0(x1), .in1(x0), .in2(not_1_out), .in3(not_1_out), .in4(a_out), .in5(not_2_out), .in6(nor_out),
    .in7(a_out), .out(multiplexer_1_out), .sel({x4, x3, x2}));
  LED led_1 (.in(multiplexer_1_out));

  // Notes on the sheet:
  //   x1x0
  //   nX0
  //   nX1nX0
  //   nNor
endmodule
