// Logisim project exp3.circ as structural Verilog: 1 circuit, main circuit main
module main (
  input  s3,
  input  s2,
  input  s1,
  input  x
);

  wire A1_out, A2_out, A3_out, A4_out, A5_out, A7_out, A8_out, A9_out, A10_out, A11_out, A12_out, A13_out,
       not_1_out, not_2_out, not_3_out, not_4_out, O3_out, O4_out, O5_out;

  not not_1 (not_1_out, s3);
  not not_2 (not_2_out, s2);
  not not_3 (not_3_out, s1);
  not not_4 (not_4_out, x);
  and A9 (A9_out, not_1_out, s2, x, not_3_out);
  and A8 (A8_out, not_1_out, s2, s1);
  and A7 (A7_out, s3, not_2_out, not_3_out);
  and A5 (A5_out, not_1_out, s2, not_3_out);
  and A4 (A4_out, s3, x);
  and A3 (A3_out, not_1_out, not_2_out, x);
  and A2 (A2_out, s3, s2);
  and A1 (A1_out, s3, s1);
  or O5 (O5_out, A9_out, A8_out, A7_out);
  and A13 (A13_out, s2, not_3_out, not_4_out);
  and A12 (A12_out, not_1_out, s2, x);
  and A11 (A11_out, s3, s1, not_4_out);
  and A10 (A10_out, not_1_out, not_2_out, s1, not_4_out);
  or O3 (O3_out, A5_out, A4_out, A3_out);
  LED led_1 (.in(O5_out));
  or O4 (O4_out, A13_out, A12_out, A11_out, A10_out);
  LED led_2 (.in(O4_out));
  LED led_3 (.in(O3_out));
  LED led_4 (.in(A2_out));
  LED led_5 (.in(A1_out));

  // Notes on the sheet:
  //   nS3
  //   nS2
  //   nS1
  //   nX
  //   o2
  //   o1
  //   n3
  //   n2
  //   n1
endmodule
