// Logisim project adder.circ as structural Verilog: 1 circuit, main circuit main
module main (
);

  wire adder_1_cout, adder_1_out, adder_2_cout, adder_2_out, adder_3_cout, adder_3_out, adder_4_cout,
       adder_4_out, adder_5_cout, adder_5_out, and_1_out, and_2_out, and_3_out, or_1_out, undriven,
       undriven_2, undriven_3, undriven_4, undriven_5, undriven_6, undriven_7, undriven_8, undriven_9,
       undriven_10, undriven_11, undriven_12, undriven_13, undriven_14, xor_1_out, xor_2_out;

  Adder #(.width(1)) adder_1 (
    .a(undriven_4), .b(undriven_5), .out(adder_1_out), .cin(undriven_14), .cout(adder_1_cout));
  Adder #(.width(1)) adder_2 (
    .a(undriven_6), .b(undriven_7), .out(adder_2_out), .cin(adder_1_cout), .cout(adder_2_cout));
  Adder #(.width(1)) adder_3 (
    .a(undriven_8), .b(undriven_9), .out(adder_3_out), .cin(adder_2_cout), .cout(adder_3_cout));
  Adder #(.width(1)) adder_4 (
    .a(undriven_10), .b(undriven_11), .out(adder_4_out), .cin(adder_3_cout), .cout(adder_4_cout));
  Adder #(.width(1)) adder_5 (
    .a(undriven_12), .b(undriven_13), .out(adder_5_out), .cin(adder_4_cout), .cout(adder_5_cout));
  and and_1 (and_1_out, undriven, undriven_2);
  and and_2 (and_2_out, undriven, undriven_3);
  and and_3 (and_3_out, undriven_2, undriven_3);
  ExactlyOne xor_1 (.out(xor_1_out), .in0(undriven), .in1(undriven_2), .in2(undriven_3));
  xor xor_2 (xor_2_out, adder_4_cout, adder_5_cout);
  or or_1 (or_1_out, and_1_out, and_2_out, and_3_out);

  // Notes on the sheet:
  //   a
  //   b
  //   ci
  //   x0
  //   y0
  //   x1
  //   y1
  //   x2
  //   y2
  //   x3
  //   y3
  //   x4
  //   y4
  //   0
  //   Cout
  //   Full Adder (FA)
  //   f0
  //   f1
  //   f2
  //   f3
  //   f4
  //   Overflow
  //   co
  //   s
endmodule
