// Logisim project comp.circ as structural Verilog: 1 circuit, main circuit main
module main (
);

  wire and_1_out, not_1_out, or_1_out, undriven, undriven_2, undriven_3;

  and and_1 (and_1_out, undriven, not_1_out);
  not not_1 (not_1_out, undriven_2);
  or or_1 (or_1_out, undriven_3, and_1_out);

  // Notes on the sheet:
  //   0
  //   x4
  //   y4
  //   Stage 4
  //   x3
  //   y3
  //   Stage 3
  //   a
  //   b
  //   x2
  //   y2
  //   in_gt
  //   Stage
  //   Stage 2
  //   out_gt
  //   x1
  //   y1
  //   Stage 1
  //   x0
  //   y0
  //   Stage 0
  //   Cout
endmodule
