// Logisim project cr.circ as structural Verilog: 1 circuit, main circuit main
module main (
);

  wire adder_2_cout, undriven_3;
  wire [4:0] adder_1_out, adder_2_out, not_1_out, undriven, undriven_4;
  wire [4:1] undriven_2;

  assign not_1_out = ~{undriven_2, undriven_2[1]};  // NOT_Gate not_1, 5 bits wide
  Adder #(.width(5)) adder_1 (.a(not_1_out), .b(undriven), .out(adder_1_out), .cin(undriven_3));  // open: cout
  Adder #(.width(5)) adder_2 (.a(adder_1_out), .b(undriven_4), .out(adder_2_out), .cout(adder_2_cout));  // open: cin

  // Notes on the sheet:
  //   00001
  //   y2
  //   y1
  //   y0
  //   0
  //   0
  //   x
  //   F
  //   Overflow
  //   Cout
endmodule
