// Logisim project fullAdder.circ as structural Verilog: 7 circuits, main circuit main
module main (
  input  [4:0] X,
  input  [4:0] Y,
  input  [1:0] S,
  output [4:0] F,
  output Cout,
  output Overflow
);

  wire Case_00_cout, Case_01_cout, Case_10_cout, Case_10_overflow, Case_11_cout, Case_11_overflow;
  wire [4:0] Case_00_f, Case_10_f, Case_11_f;

  mulp Case_00 (.X(X), .Y(Y), .Cout(Case_00_cout), .F(Case_00_f));
  comp Case_01 (.X(X), .Y(Y), .Cout(Case_01_cout));
  adder Case_10 (.X(X), .Y(Y), .Cout(Case_10_cout), .F(Case_10_f), .Overflow(Case_10_overflow));
  sub Case_11 (.X(X), .Y(Y), .Cout(Case_11_cout), .F(Case_11_f), .Overflow(Case_11_overflow));
  Multiplexer #(.select(2), .width(5), .enable("false")) multiplexer_1 (
    .in0(Case_00_f), .in1({5{1'b0}}), .in2(Case_10_f), .in3(Case_11_f), .out(F), .sel(S));
  Multiplexer #(.select(2), .enable("false")) multiplexer_2 (
    .in0(Case_00_cout), .in1(Case_01_cout), .in2(Case_10_cout), .in3(Case_11_cout), .out(Cout), .sel(S));
  Multiplexer #(.select(2), .enable("false")) multiplexer_3 (
    .in0(1'b0), .in1(1'b0), .in2(Case_10_overflow), .in3(Case_11_overflow), .out(Overflow), .sel(S));
endmodule

// FA
module fullAdder (
  input  a,
  input  b,
  input  ci,
  output co,
  output s
);

  wire and_1_out, and_2_out, and_3_out, xor_1_out;

  and and_1 (and_1_out, a, b);
  and and_2 (and_2_out, a, ci);
  and and_3 (and_3_out, b, ci);
  xor xor_1 (xor_1_out, a, b);
  or or_1 (co, and_1_out, and_2_out, and_3_out);
  xor xor_2 (s, xor_1_out, ci);

  // Notes on the sheet:
  //   Full Adder
  //   FA
endmodule

// Adder
module adder (
  input  [4:0] X,
  input  [4:0] Y,
  output [4:0] F,
  output Overflow,
  output Cout
);

  wire fulladder_1_co, fulladder_2_co, fulladder_3_co, fulladder_4_co;

  fullAdder fulladder_1 (.a(X[0]), .b(Y[0]), .ci(1'b0), .co(fulladder_1_co), .s(F[0]));
  fullAdder fulladder_2 (.a(X[1]), .b(Y[1]), .ci(fulladder_1_co), .co(fulladder_2_co), .s(F[1]));
  fullAdder fulladder_3 (.a(X[2]), .b(Y[2]), .ci(fulladder_2_co), .co(fulladder_3_co), .s(F[2]));
  fullAdder fulladder_4 (.a(X[3]), .b(Y[3]), .ci(fulladder_3_co), .co(fulladder_4_co), .s(F[3]));
  fullAdder fulladder_5 (.a(X[4]), .b(Y[4]), .ci(fulladder_4_co), .co(Cout), .s(F[4]));
  xor xor_1 (Overflow, fulladder_4_co, Cout);

  // Notes on the sheet:
  //   Case10
  //   Adder
endmodule

module mulp (
  input  [4:0] X,
  input  [4:0] Y,
  output [4:0] F,
  output Cout
);

  wire [2:0] and_1_out;
  wire [3:0] adder_1_out;
  wire [3:1] and_2_out;
  wire [4:2] and_3_out;
  wire [4:4] adder_1_cout;

  and and_1 (and_1_out[0], X[1], Y[0]);
  and and_2 (and_2_out[1], X[2], Y[0]);
  and and_3 (and_3_out[2], X[3], Y[0]);
  and and_4 (and_1_out[1], X[1], Y[1]);
  and and_5 (and_2_out[2], X[2], Y[1]);
  and and_6 (and_3_out[3], X[3], Y[1]);
  and and_7 (and_1_out[2], X[1], Y[2]);
  and and_8 (and_2_out[3], X[2], Y[2]);
  and and_9 (and_3_out[4], X[3], Y[2]);
  Adder #(.width(4)) adder_1 (
    .a({1'b0, and_1_out}), .b({and_2_out, 1'b0}), .out(adder_1_out), .cin(1'b0), .cout(adder_1_cout[4]));
  adder adder_2 (.X({adder_1_cout[4], adder_1_out}), .Y({and_3_out, 2'b00}), .Cout(Cout), .F(F));  // open: Overflow

  // Notes on the sheet:
  //   Case00
endmodule

// stage
module compStage (
  input  in_gt,
  input  a,
  input  b,
  input  in_eq,
  output out_gt,
  output out_eq
);

  wire and_1_out, not_1_out, xnor_1_out;

  not not_1 (not_1_out, b);
  and and_1 (and_1_out, a, not_1_out, in_eq);
  xnor xnor_1 (xnor_1_out, a, b);
  or or_1 (out_gt, in_gt, and_1_out);
  and and_2 (out_eq, xnor_1_out, in_eq);

  // Notes on the sheet:
  //   Stage
endmodule

module comp (
  input  [4:0] X,
  input  [4:0] Y,
  output Cout
);

  wire compstage_1_out_eq, compstage_1_out_gt, compstage_2_out_eq, compstage_2_out_gt, compstage_3_out_eq,
       compstage_3_out_gt, compstage_4_out_eq, compstage_4_out_gt;

  compStage compstage_1 (
    .in_gt(1'b0), .a(X[4]), .b(Y[4]), .in_eq(1'b1), .out_gt(compstage_1_out_gt), .out_eq(compstage_1_out_eq));
  compStage compstage_2 (
    .in_gt(compstage_1_out_gt), .a(X[3]), .b(Y[3]), .in_eq(compstage_1_out_eq), .out_gt(compstage_2_out_gt),
    .out_eq(compstage_2_out_eq));
  compStage compstage_3 (
    .in_gt(compstage_2_out_gt), .a(X[2]), .b(Y[2]), .in_eq(compstage_2_out_eq), .out_gt(compstage_3_out_gt),
    .out_eq(compstage_3_out_eq));
  compStage compstage_4 (
    .in_gt(compstage_3_out_gt), .a(X[1]), .b(Y[1]), .in_eq(compstage_3_out_eq), .out_gt(compstage_4_out_gt),
    .out_eq(compstage_4_out_eq));
  compStage compstage_5 (
    .in_gt(compstage_4_out_gt), .a(X[0]), .b(Y[0]), .in_eq(compstage_4_out_eq), .out_gt(Cout));  // open: out_eq

  // Notes on the sheet:
  //   Case01
endmodule

module sub (
  input  [4:0] X,
  input  [4:0] Y,
  output [4:0] F,
  output Overflow,
  output Cout
);

  wire [4:0] adder_1_f, not_1_out;

  assign not_1_out = ~{Y[2:0], 2'b00};  // NOT_Gate not_1, 5 bits wide
  adder adder_1 (.X(not_1_out), .Y(5'b00001), .F(adder_1_f));  // open: Cout, Overflow
  adder adder_2 (.X(adder_1_f), .Y(X), .Cout(Cout), .F(F), .Overflow(Overflow));

  // Notes on the sheet:
  //   Case11
endmodule
