// Logisim project mulp.circ as structural Verilog: 1 circuit, main circuit main
module main (
  input  y0,
  input  y1,
  input  y2,
  input  x1,
  input  x2,
  input  x3
);

  wire adder_2_cout, undriven_3, undriven_4;
  wire [3:0] adder_1_out, and_1_out, undriven;
  wire [4:0] adder_2_out, undriven_2;
  wire [4:4] adder_1_cout;

  and and_1 (and_1_out[0], x1, y0);
  and and_2 (undriven[1], x2, y0);
  and and_3 (undriven_2[2], x3, y0);
  and and_4 (and_1_out[1], x1, y1);
  and and_5 (undriven[2], x2, y1);
  and and_6 (undriven_2[3], x3, y1);
  and and_7 (and_1_out[2], x1, y2);
  and and_8 (undriven[3], x2, y2);
  and and_9 (undriven_2[4], x3, y2);
  Adder #(.width(4)) adder_1 (.a(and_1_out), .b(undriven), .out(adder_1_out), .cin(undriven_3), .cout(adder_1_cout[4]));
  Adder #(.width(5)) adder_2 (
    .a({adder_1_cout[4], adder_1_out}), .b(undriven_2), .out(adder_2_out), .cin(undriven_4),
    .cout(adder_2_cout));

  // Notes on the sheet:
  //   0
  //   0
  //   0
  //   0
  //   0
  //   FA
  //   0
  //   Cout
  //   FA
  //   F
endmodule
